# Fritzing sketch project2_wiring (saved by Fritzing 0.9.3b)

parts:
  S1 = H-Bridge with L298N
  M1 = DC Motor
  M2 = DC Motor
  VCC1 = Battery block 9V
  U1 = SWITCH-SPST-2 [package=switch-spst-vertical]
  hc-sr1 = hc-sr04
  Part1 = Arduino Uno (Rev3)
  J2 = Basic Servo with reading
  IR1 = TSOP312.., 314.. [package=THT]

nets:
  N1: S1.12V, U1.O
  GND: S1.GND, VCC1.-, hc-sr1.GND, Part1.GND, IR1.GND
  N2: S1.ENA, Part1.D6_PWM
  N3: S1.IN1, Part1.D13/SCK
  N4: S1.IN2, Part1.D12/MISO
  N5: S1.IN3, Part1.D3_PWM
  N6: S1.IN4, Part1.D4
  N7: S1.ENB, Part1.D5_PWM
  N8: S1.M1-01, M2.pin_1
  N9: S1.M1-02, M2.pin_2
  N10: S1.M2-01, M1.pin_2
  N11: S1.M2-02, M1.pin_1
  N12: VCC1.+, U1.P, Part1.VIN
  VCC: hc-sr1.VCC, Part1.5V, J2.vcc, IR1.Vs
  N13: hc-sr1.Trig, Part1.D7
  N14: hc-sr1.Echo, Part1.D8
  N15: Part1.A0, J2.pot
  N16: Part1.D11_PWM/MOSI, J2.pulse
  N17: Part1.D2, IR1.Data

custom parts:
  H-Bridge with L298N: h-bridge
  Basic Servo with reading: A generic servo.
